# Fritzing sketch AR25_2LED (saved by Fritzing 0.9.3b)
breadboards: 1

parts:
  부품1 = Arduino Uno (Rev3)
  LED2 = LED - 5mm [color="Red (633nm)" package="5 mm [THT]"]
  LED3 = smd LED [color="Green (560nm)" package="1206 [SMD]"]
  R2 = Resistor [tolerance=±5% resistance=330 package=THT]
  R3 = Resistor [tolerance=±5% resistance=330 package=THT]

nets:
  N1: 부품1.GND, R2.Pin_1, R3.Pin_0
  N2: 부품1.D5_PWM, LED3.anode
  N3: LED2.cathode, R3.Pin_1
  N4: LED3.cathode, R2.Pin_0
