# Fritzing sketch AR25_4led (saved by Fritzing 0.9.3b)
breadboards: 1

parts:
  LED1 = LED - 5mm [color="Red (633nm)" package="5 mm [THT]"]
  LED2 = LED - 5mm [color="Green (570nm)" package="5 mm [THT]"]
  LED3 = LED - 5mm [color="Blue (470nm)" package="5 mm [THT]"]
  LED4 = LED - 5mm [color="Yellow (585nm)" package="5 mm [THT]"]
  R1 = Resistor [tolerance=±5% resistance=330 package=THT]
  R2 = Resistor [tolerance=±5% resistance=330 package=THT]
  R3 = Resistor [tolerance=±5% resistance=330 package=THT]
  R4 = Resistor [tolerance=±5% resistance=330 package=THT]
  부품1 = Arduino Uno (Rev3)

nets:
  N1: LED1.cathode, R4.Pin_1
  N2: LED1.anode, 부품1.D3_PWM
  N3: LED2.cathode, R1.Pin_0
  N4: LED2.anode, 부품1.D5_PWM
  N5: LED3.cathode, R3.Pin_0
  N6: LED3.anode, 부품1.D6_PWM
  N7: LED4.cathode, R2.Pin_0
  N8: LED4.anode, 부품1.D9_PWM
  N9: R1.Pin_1, R2.Pin_1, R3.Pin_1, R4.Pin_0, 부품1.GND
