# Fritzing sketch AR25_RGB (saved by Fritzing 0.9.3b)
breadboards: 1

parts:
  LED1 = Super Flux RGB LED (com. anode)
  부품1 = Arduino Uno (Rev3)

nets:
  N1: LED1.red_cathode, 부품1.D3_PWM
  N2: LED1.blue_cathode, 부품1.D6_PWM
  N3: LED1.green_cathode, 부품1.D5_PWM
  N4: LED1.common_anode, 부품1.GND
