# Fritzing sketch 신호등_회로도 (saved by Fritzing 0.9.3b)
breadboards: 1

parts:
  부품1 = Arduino Uno (Rev3)
  LED1 = LED - 5mm [color="Green (555nm)" package="5 mm [THT]"]
  LED2 = LED - 5mm [color="Red (633nm)" package="5 mm [THT]"]
  LED3 = LED - 5mm [color="Red (633nm)" package="5 mm [THT]"]
  LED4 = LED - 5mm [color="Green (555nm)" package="5 mm [THT]"]
  LED5 = LED - 5mm [color="Orange (620nm)" package="5 mm [THT]"]
  R1 = Resistor [tolerance=±5% resistance=220 package=THT]
  R2 = Resistor [tolerance=±5% resistance=220 package=THT]
  R3 = Resistor [tolerance=±5% resistance=220 package=THT]
  R4 = Resistor [tolerance=±5% resistance=220 package=THT]
  R5 = Resistor [tolerance=±5% resistance=220 package=THT]
  R6 = Resistor [tolerance=±5% resistance=220 package=THT]
  7_Segment1 = 7 Segment Display
  U1 = 74HC595 [package="DIP16 [THT]"]
  R7 = Resistor [tolerance=±5% resistance=220 package=THT]
  R8 = Resistor [tolerance=±5% resistance=220 package=THT]
  R9 = Resistor [tolerance=±5% resistance=220 package=THT]
  R10 = Resistor [tolerance=±5% resistance=220 package=THT]
  R11 = Resistor [tolerance=±5% resistance=220 package=THT]
  R12 = Resistor [tolerance=±5% resistance=220 package=THT]
  R13 = Resistor [tolerance=±5% resistance=220 package=THT]
  8x8_LED_Modul_mit_MAX1 = 8x8 LED Modul mit MAX7219 [package=THT]

nets:
  N1: 부품1.D9_PWM, U1.Q3, U1.DS, R13.Pin_0
  N2: 부품1.D10_PWM/SS, U1.Q6, U1.SH_CP, R9.Pin_0
  N3: 부품1.D11_PWM/MOSI, U1.Q5, U1.ST_CP, R8.Pin_0
  N4: 부품1.D12/MISO, R2.Pin_0
  N5: 부품1.D13/SCK, R1.Pin_0
  GND: 부품1.GND, LED1.cathode, LED2.cathode, LED3.cathode, LED4.cathode, LED5.cathode, 7_Segment1.common_anode, U1.Q4, U1.GND, U1.Q7', U1.OE, R11.Pin_0, 8x8_LED_Modul_mit_MAX1.GND_Eingang
  N6: 부품1.D2, 8x8_LED_Modul_mit_MAX1.CS_Eingang
  N7: 부품1.D3_PWM, 8x8_LED_Modul_mit_MAX1.CLK_Eingang
  N8: 부품1.D4, 8x8_LED_Modul_mit_MAX1.DIN_Eingang
  N9: 부품1.D5_PWM, R5.Pin_0
  N10: 부품1.D6_PWM, R4.Pin_0
  N11: 부품1.D7, R3.Pin_0
  N12: LED1.anode, R2.Pin_1
  N13: LED2.anode, R1.Pin_1
  N14: LED3.anode, R3.Pin_1
  N15: LED4.anode, R5.Pin_1
  N16: LED5.anode, R4.Pin_1
  N17: R6.Pin_0, 7_Segment1.Segment_B
  N18: R6.Pin_1, U1.Q1, U1.Q7, U1.MR, U1.VCC, 8x8_LED_Modul_mit_MAX1.VCC_Eingang
  N19: 7_Segment1.Segment_E, R11.Pin_1
  N20: 7_Segment1.Segment_D, R13.Pin_1
  N21: 7_Segment1.Segment_C, R12.Pin_0
  N22: 7_Segment1.Segment_DP, R10.Pin_0
  N23: 7_Segment1.Segment_A, R7.Pin_0
  N24: 7_Segment1.Segment_F, R8.Pin_1
  N25: 7_Segment1.Segment_G, R9.Pin_1
  N26: U1.Q2, U1.Q0, R7.Pin_1, R12.Pin_1
